# Fritzing sketch Car Circuit (saved by Fritzing 0.9.3b)
circuit board: 8.46667cm x 5.64444cm
breadboards: 1

parts:
  Part1 = Arduino Mega 2560 (Rev3)
  U2 = ESP8266 WiFi Module [part_number=ESP8266]
  Part2 = Logic Level Converter  # not connected
  U3 = LIPO-2000mAh [package=lipo-2000]
  U4 = L298 [package=multiwatt15]
  C1 = Tantalum Capacitor [capacitance=1nF package="100 mil [THT, tantalum]"]
  C2 = Electrolytic Capacitor [capacitance=0.1mF package="100 mil [THT, electrolytic]"]
  C3 = Electrolytic Capacitor [capacitance=0.1mF package="100 mil [THT, electrolytic]"]
  C4 = Tantalum Capacitor [capacitance=1nF package="100 mil [THT, tantalum]"]
  D1 = Rectifier Diode [part_number=1N4001 package="300 mil [THT]"]
  D2 = Rectifier Diode [part_number=1N4001 package="300 mil [THT]"]
  D3 = Rectifier Diode [part_number=1N4001 package="300 mil [THT]"]
  D4 = Rectifier Diode [part_number=1N4001 package="300 mil [THT]"]
  M1 = DC Motor
  M2 = DC Motor
  M3 = DC Motor
  M4 = DC Motor
  R1 = Resistor [tolerance=±5% resistance=10k package=THT]
  R2 = Resistor [tolerance=±5% resistance=10k package=THT]

nets:
  3V3: Part1.3V3, U2.3.3V, R1.Pin_1, R2.Pin_1
  N1: Part1.5V, U4.VLS, C1.+, C2.-
  N2: Part1.GND, U3.+, U4.VS, C1.-, C2.+, C3.-, C4.+, D1.cathode, D2.cathode, D3.cathode, D4.cathode
  N3: Part1.D3_PWM, U4.ENA
  N4: Part1.D4_PWM, Part1.D52, U4.IN3, U4.ENB
  N5: Part1.D50, U4.IN1
  N6: Part1.D51, U4.IN2
  N7: Part1.D53, U4.IN4
  GND: U2.GND, U3.-, U4.CSA, U4.GND, U4.CSB, C3.+, C4.-
  N8: U2.RST, R1.Pin_0
  N9: U2.CHIP_EN, R2.Pin_0
  N10: U4.OUT1, M1.pin_1, M2.pin_2
  N11: U4.OUT2, M1.pin_2, M2.pin_1
  N12: U4.OUT3, D2.anode, M3.pin_1, M4.pin_2
  N13: U4.OUT4, D1.anode, M3.pin_2, M4.pin_1
